// Logisim project CPU.circ as structural Verilog: 1 circuit, main circuit main
module main (
  input  in_1
);

  wire and_1_out, and_2_out, and_3_out, and_4_out, clock_1_out, counter_1_q, decoder_1_out0, decoder_1_out1,
       decoder_1_out2, decoder_1_out8, decoder_1_out9, not_1_out, or_1_out, or_2_out, or_3_out;
  wire [3:0] bit_extender_1_out, IR_q;
  wire [7:0] adder_1_out, multiplexer_1_out, multiplexer_2_out, multiplexer_3_out, PC_q, R_A_q, R_B_q,
       ram_1_data, subtractor_1_out, undriven;

  Clock clock_1 (.out(clock_1_out));
  Counter PC (.count(not_1_out), .Q(PC_q), .clk(clock_1_out));  // open: load, D, carry, clr
  Bit_Extender #(.out_width(4)) bit_extender_1 (.in(undriven), .out(bit_extender_1_out));
  Multiplexer #(.width(8), .enable("false")) multiplexer_1 (
    .in0(PC_q), .in1(undriven), .out(multiplexer_1_out), .sel(and_4_out));
  Decoder #(.select(4), .enable("false")) decoder_1 (
    .out0(decoder_1_out0), .out1(decoder_1_out1), .out2(decoder_1_out2), .out8(decoder_1_out8),
    .out9(decoder_1_out9), .sel(IR_q));  // open: out3, out4, out5, out6, out7, out10, out11, out12, out13, out14, out15
  and and_1 (and_1_out, decoder_1_out2, counter_1_q);
  or or_1 (or_1_out, decoder_1_out0, decoder_1_out8);
  and and_2 (and_2_out, decoder_1_out1, counter_1_q);
  RAM ram_1 (.addr(multiplexer_1_out), .data(ram_1_data), .sel(in_1), .ld(and_1_out));  // open: clk, clr
  or or_2 (or_2_out, decoder_1_out0, decoder_1_out1, decoder_1_out2);
  and and_3 (and_3_out, or_1_out, counter_1_q);
  Multiplexer #(.width(8), .enable("false")) multiplexer_2 (
    .in0(ram_1_data), .in1(multiplexer_3_out), .out(multiplexer_2_out), .sel(or_3_out));
  or or_3 (or_3_out, decoder_1_out8, decoder_1_out9);
  assign ram_1_data = and_1_out ? R_A_q : 8'bz;  // Controlled_Buffer controlled_buffer_1
  Register R_A (.D(multiplexer_2_out), .en(and_3_out), .Q(R_A_q), .clk(clock_1_out));  // open: clr
  and and_4 (and_4_out, counter_1_q, or_2_out);
  Register R_B (.D(multiplexer_2_out), .en(and_2_out), .Q(R_B_q), .clk(clock_1_out));  // open: clr
  Counter #(.width(1), .max('h1)) counter_1 (.Q(counter_1_q), .clk(clock_1_out));  // open: load, D, count, carry, clr
  Adder adder_1 (.a(R_A_q), .b(R_B_q), .out(adder_1_out));  // open: cin, cout
  not not_1 (not_1_out, counter_1_q);
  Register IR (.D(ram_1_data), .en(not_1_out), .Q({IR_q, bit_extender_1_out}), .clk(clock_1_out));  // open: clr
  Multiplexer #(.width(8), .enable("false")) multiplexer_3 (
    .in0(adder_1_out), .in1(subtractor_1_out), .out(multiplexer_3_out), .sel(decoder_1_out9));
  Subtractor subtractor_1 (.a(R_A_q), .b(R_B_q), .out(subtractor_1_out));  // open: bin, bout
endmodule
