// Logisim project CPU_8_bits.circ as structural Verilog: 1 circuit, main circuit main
module main (
  input  [1:0] in_1,
  input  [1:0] in_2,
  input  in_3,
  input  in_4,
  input  in_5,
  input  in_6,
  output out_7,
  output [2:0] out_8,
  output out_9,
  output out_10,
  output [2:0] out_11,
  output out_12,
  output [2:0] out_13,
  output [2:0] out_14,
  output out_15,
  output [2:0] out_16,
  output out_17,
  output out_18,
  output out_19,
  output out_20,
  output [2:0] out_21
);

  wire and_3_out, and_4_out, and_5_out, button_1_out, button_2_out, button_3_out, d_ff_1_q, d_ff_2_q,
       d_ff_3_q, d_ff_4_q, d_ff_5_q, d_ff_6_q, multiplexer_2_out, multiplexer_5_out, multiplexer_7_out,
       not_2_out, not_3_out, or_3_out, or_4_out, or_5_out;
  wire [2:0] multiplexer_1_out, multiplexer_3_out, multiplexer_4_out, multiplexer_6_out, ram_1_data;

  or or_1 (out_7, in_2[1], in_1[1]);
  or or_2 (out_8[0], in_1[0], in_2[0]);
  and and_1 (out_10, in_2[1], in_1[1]);
  and and_2 (out_11[0], in_2[0], in_1[0]);
  Adder #(.width(2)) adder_1 (.a(in_1), .b(in_2), .out(out_14[1:0]), .cout(out_14[2]));  // open: cin
  Subtractor #(.width(2)) subtractor_1 (.a(in_1), .b(in_2), .out(out_16[1:0]), .bout(out_16[2]));  // open: bin
  Comparator #(.width(2), .mode("unsigned")) comparator_1 (.a(in_1), .b(in_2), .gt(out_18), .eq(out_19), .lt(out_20));
  assign out_13[1:0] = ~in_2;  // NOT_Gate not_1, 2 bits wide
  Button button_1 (.out(button_1_out));
  Button button_2 (.out(button_2_out));
  Button button_3 (.out(button_3_out));
  RAM #(.addrWidth(4), .dataWidth(3)) ram_1 (
    .addr({in_2, in_1}), .data(ram_1_data), .sel(1'b1), .clk(button_1_out), .ld(in_3), .clr(and_4_out));
  Multiplexer #(.width(3), .enable("false")) multiplexer_1 (
    .in0({1'b0, out_7, out_8[0]}), .in1({1'b0, out_10, out_11[0]}), .out(multiplexer_1_out), .sel(or_3_out));
  or or_3 (or_3_out, multiplexer_2_out, multiplexer_5_out, multiplexer_7_out);
  Multiplexer #(.enable("false")) multiplexer_2 (.in0(in_4), .in1(d_ff_1_q), .out(multiplexer_2_out), .sel(in_3));
  Multiplexer #(.width(3), .enable("false")) multiplexer_3 (
    .in0(multiplexer_1_out), .in1({1'b0, out_13[1:0]}), .out(multiplexer_3_out), .sel(or_5_out));
  and and_3 (and_3_out, not_2_out, multiplexer_5_out, multiplexer_7_out);
  not not_2 (not_2_out, multiplexer_2_out);
  Multiplexer #(.width(3), .enable("false")) multiplexer_4 (
    .in0(multiplexer_3_out), .in1(out_14), .out(multiplexer_4_out), .sel(or_4_out));
  or or_4 (or_4_out, and_3_out, multiplexer_2_out);
  or or_5 (or_5_out, multiplexer_2_out, multiplexer_5_out);
  not not_3 (not_3_out, multiplexer_5_out);
  and and_4 (and_4_out, multiplexer_2_out, multiplexer_5_out, multiplexer_7_out);
  Multiplexer #(.enable("false")) multiplexer_5 (.in0(in_5), .in1(d_ff_3_q), .out(multiplexer_5_out), .sel(in_3));
  Multiplexer #(.width(3), .enable("false")) multiplexer_6 (
    .in0(multiplexer_4_out), .in1(out_16), .out(multiplexer_6_out), .sel(multiplexer_2_out));
  Multiplexer #(.enable("false")) multiplexer_7 (.in0(in_6), .in1(d_ff_5_q), .out(multiplexer_7_out), .sel(in_3));
  Multiplexer #(.width(3), .enable("false")) multiplexer_8 (
    .in0(multiplexer_6_out), .in1({out_18, out_19, out_20}), .out(out_21), .sel(and_5_out));
  and and_5 (and_5_out, multiplexer_2_out, not_3_out, multiplexer_7_out);
  D_Flip_Flop d_ff_1 (.clk(button_2_out), .D(ram_1_data[2]), .Q(d_ff_1_q), .en(1'b1));  // open: Qn, preset, reset
  D_Flip_Flop d_ff_2 (.clk(button_3_out), .D(out_21[2]), .Q(d_ff_2_q), .en(1'b1));  // open: Qn, preset, reset
  D_Flip_Flop d_ff_3 (.clk(button_2_out), .D(ram_1_data[1]), .Q(d_ff_3_q), .en(1'b1));  // open: Qn, preset, reset
  D_Flip_Flop d_ff_4 (.clk(button_3_out), .D(out_21[1]), .Q(d_ff_4_q), .en(1'b1));  // open: Qn, preset, reset
  Transistor transistor_1 (.in(d_ff_4_q), .out(ram_1_data[1]), .gate(in_3));
  Transistor transistor_2 (.in(d_ff_2_q), .out(ram_1_data[2]), .gate(in_3));
  D_Flip_Flop d_ff_5 (.clk(button_2_out), .D(ram_1_data[0]), .Q(d_ff_5_q), .en(1'b1));  // open: Qn, preset, reset
  D_Flip_Flop d_ff_6 (.clk(button_3_out), .D(out_21[0]), .Q(d_ff_6_q), .en(1'b1));  // open: Qn, preset, reset
  Transistor transistor_3 (.in(d_ff_6_q), .out(ram_1_data[0]), .gate(in_3));

  assign out_8[2:1] = {1'b0, out_7};
  assign out_9 = out_8[0];
  assign out_11[2:1] = {1'b0, out_10};
  assign out_12 = out_11[0];
  assign out_13[2] = 1'b0;
  assign out_15 = out_14[2];
  assign out_17 = out_16[2];

  // Notes on the sheet:
  //   Entrada A0 y A1 ->
  //   Bit para cambiar de escritura a lectura ->
  //   Registro de datos
  //   000 Operación logica OR
  //   001 Operación logica AND
  //   010 Negación de B0 y B1
  //   011 Suma Aritmetica
  //   100 Resta Aritmetica
  //   101 Comparador
  //   Boton para leer o guardar datos
  //   Boton para guardar temporalmente el registro de la cache
  //   Boton para guardar temporalmente la salida de datos
  //   <-Entrada B0 y B1
  //   Salida de datos ->
  //   111 Borrar Memoria Cache
endmodule
